# Fritzing sketch Wiring-Direct (saved by Fritzing 0.9.3b)

parts:
  Part1 = Arduino Uno (Rev3)
  LED1 = LED - 5mm [color="Red (660nm)" package="5 mm [THT]"]
  LED2 = LED - 5mm [color="Red (660nm)" package="5 mm [THT]"]
  LED3 = LED - 5mm [color="Blue (505nm)" package="5 mm [THT]"]
  LED4 = LED - 5mm [color="Blue (505nm)" package="5 mm [THT]"]
  R2 = Resistor [tolerance=±5% resistance=220 package=THT]  # not connected
  LED5 = LED - 5mm [color="Red (660nm)" package="5 mm [THT]"]
  LED6 = LED - 5mm [color="Blue (505nm)" package="5 mm [THT]"]
  LED7 = LED - 5mm [color="Blue (505nm)" package="5 mm [THT]"]
  LED8 = LED - 5mm [color="Red (660nm)" package="5 mm [THT]"]
  R3 = Resistor [tolerance=±5% resistance=220 package=THT]  # not connected
  R4 = Resistor [tolerance=±5% resistance=220 package=THT]  # not connected
  R5 = Resistor [tolerance=±5% resistance=220 package=THT]  # not connected
  R6 = Resistor [tolerance=±5% resistance=220 package=THT]  # not connected
  R7 = Resistor [tolerance=±5% resistance=220 package=THT]  # not connected
  R8 = Resistor [tolerance=±5% resistance=220 package=THT]  # not connected
  R9 = Resistor [tolerance=±5% resistance=220 package=THT]  # not connected
  LED9 = LED - 5mm [color="Red (635nm)" package="5 mm [THT]"]  # not connected
  LED10 = LED - 5mm [color="Red (635nm)" package="5 mm [THT]"]
  LED11 = LED - 5mm [color="Orange (605nm)" package="5 mm [THT]"]
  LED12 = LED - 5mm [color="Orange (605nm)" package="5 mm [THT]"]
  LED13 = LED - 5mm [color="Orange (605nm)" package="5 mm [THT]"]
  LED14 = LED - 5mm [color="Orange (605nm)" package="5 mm [THT]"]
  R10 = Resistor [tolerance=±5% resistance=220 package=THT]  # not connected
  R11 = Resistor [tolerance=±5% resistance=220 package=THT]  # not connected
  R12 = Resistor [tolerance=±5% resistance=220 package=THT]  # not connected
  R13 = Resistor [tolerance=±5% resistance=220 package=THT]  # not connected
  R14 = Resistor [tolerance=±5% resistance=220 package=THT]  # not connected
  R15 = Resistor [tolerance=±5% resistance=220 package=THT]  # not connected
  LED15 = LED - 5mm [color="Green (555nm)" package="5 mm [THT]"]
  R16 = Resistor [tolerance=±5% resistance=220 package=THT]  # not connected
  R17 = Resistor [tolerance=±5% resistance=220 package=THT]  # not connected
  LED16 = LED - 5mm [color="Green (555nm)" package="5 mm [THT]"]
  R18 = Resistor [tolerance=±5% resistance=220 package=THT]
  LED17 = LED - 5mm [color="Yellow (595nm)" package="5 mm [THT]"]  # not connected
  R19 = Resistor [tolerance=±5% resistance=220 package=THT]  # not connected
  LED18 = LED - 5mm [color="Yellow (595nm)" package="5 mm [THT]"]
  R20 = Resistor [tolerance=±5% resistance=220 package=THT]  # not connected
  LED19 = LED - 5mm [color="Yellow (595nm)" package="5 mm [THT]"]  # not connected
  R21 = Resistor [tolerance=±5% resistance=220 package=THT]  # not connected
  LED20 = LED - 5mm [color="Yellow (595nm)" package="5 mm [THT]"]

nets:
  N1: Part1.A0, LED11.anode
  N2: Part1.A1, LED12.anode
  N3: Part1.A2, LED13.anode
  N4: Part1.A3, LED14.anode
  N5: Part1.A4/SDA, LED10.anode
  N6: Part1.D8, LED8.anode
  N7: Part1.D9_PWM, LED5.anode
  N8: Part1.D10_PWM/SS, LED15.anode
  N9: Part1.D11_PWM/MOSI, LED18.anode
  N10: Part1.D12/MISO, LED16.anode
  N11: Part1.D13/SCK, LED20.anode
  N12: Part1.D2, LED4.anode
  N13: Part1.D3_PWM, LED3.anode
  N14: Part1.D4, LED1.anode
  N15: Part1.D5_PWM, LED2.anode
  N16: Part1.D6_PWM, LED7.anode
  N17: Part1.D7, LED6.anode
  N18: Part1.GND, R18.Pin_1

notes:
  P1 Start/Menu
  P2 Start/Menu
  Cabinet Marquee/Bass Lights
  P1 Pad
  P2 Pad
