# Fritzing sketch Wiring-MOSFET (saved by Fritzing 0.9.3b)
breadboards: 1

parts:
  R1 = Resistor [tolerance=±5% resistance=10k package=THT]
  Q1 = Basic FET N-Channel [package="TO220 [THT]"]
  JP1 = Header 1 [package=1x01_offset]
  JP2 = Header 1 [package=1x01_offset]
  Part1 = Arduino Uno (Rev3)
  JP4 = Header 1 [package=1x01_offset]
  JP5 = Header 1 [package=1x01_offset]

nets:
  N1: R1.Pin_0, Q1.gate, Part1.D2
  N2: R1.Pin_1, Q1.source, JP1.1, Part1.GND
  N3: Q1.drain, JP5.1
  N4: JP2.1, JP4.1

notes:
  Wire MOSFET's "Gate" pin to Arduino/Shift Register output
  Use 1 MOSFET for each high-power light to control
  10k resistor
  To LED power supply
  For high-power LED modules/CCFLs/etc:
  +V
  GND
  To LED module
  +V  GND
