# Fritzing sketch Wiring-ShiftRegisters (saved by Fritzing 0.9.3b)
breadboards: 1

parts:
  Part1 = Arduino Uno (Rev3)
  U2 = 74HC595 [package="DIP16 [THT]"]
  U3 = 74HC595 [package="DIP16 [THT]"]
  U4 = 74HC595 [package="DIP16 [THT]"]
  U5 = 74HC595 [package="DIP16 [THT]"]
  U6 = Header 8 [package=1x08_smd]
  U7 = Header 8 [package=1x08_smd]
  U8 = Header 8 [package=1x08_smd]
  U9 = Header 8 [package=1x08_smd]

nets:
  N1: Part1.D2, U2.SH_CP, U3.SH_CP, U4.SH_CP, U5.SH_CP
  N2: Part1.D3_PWM, U2.DS
  N3: Part1.D4, U2.ST_CP, U3.ST_CP, U4.ST_CP, U5.ST_CP
  VCC: Part1.5V, U2.MR, U2.VCC, U3.MR, U3.VCC, U4.MR, U4.VCC, U5.Q7', U5.VCC
  GND: Part1.GND, U2.GND, U2.OE, U3.GND, U3.OE, U4.GND, U4.OE, U5.GND, U5.OE
  N4: U2.Q1, U6.2
  N5: U2.Q2, U6.3
  N6: U2.Q3, U6.4
  N7: U2.Q4, U6.5
  N8: U2.Q5, U6.6
  N9: U2.Q6, U6.7
  N10: U2.Q7, U6.8
  N11: U2.Q7', U3.DS
  N12: U2.Q0, U6.1
  N13: U3.Q1, U7.2
  N14: U3.Q2, U7.3
  N15: U3.Q3, U7.4
  N16: U3.Q4, U7.5
  N17: U3.Q5, U7.6
  N18: U3.Q6, U7.7
  N19: U3.Q7, U7.8
  N20: U3.Q7', U4.DS
  N21: U3.Q0, U7.1
  N22: U4.Q1, U8.2
  N23: U4.Q2, U8.3
  N24: U4.Q3, U8.4
  N25: U4.Q4, U8.5
  N26: U4.Q5, U8.6
  N27: U4.Q6, U8.7
  N28: U4.Q7, U8.8
  N29: U4.Q7', U5.DS
  N30: U4.Q0, U8.1
  N31: U5.Q1, U9.2
  N32: U5.Q2, U9.3
  N33: U5.Q3, U9.4
  N34: U5.Q4, U9.5
  N35: U5.Q5, U9.6
  N36: U5.Q6, U9.7
  N37: U5.Q7, U9.8
  N38: U5.Q0, U9.1

notes:
  Note: You can modify the code to change which lights are on which shift registers
  You don't need to wire up all 4 shift registers if you don't need them
  (Having 4 is only needed if you want more lights than most people would want :P)
  P1 Gameplay
  P2 Gameplay
  Cabinet lights
  Etc lights
  SM Gameplay Lights 0-7 mapped to the P1/P2 registers
  (Their pinouts depend on what game mode you play)
  From left to right:
  4x marquee lights, P1 Start/Menu,
  P2 Start/Menu
  Leftmost pin is the bass neon
  All others are free for code
  (See README.MD for a link to the mappings)
  mods/expansion
